# Fritzing sketch SMcounter_circuit (saved by Fritzing 0.9.4)
circuit board: 8.46667cm x 5.64444cm

parts:
  WeMos_D1_Mini1 = WeMos D1 Mini
  Q1 = LTR-301 [package=ltr-301]
  Q2 = LTR-301 [package=ltr-301]
  D1 = Rectifier Diode [part_number=1N4001 package="300 mil [THT]"]
  D2 = Rectifier Diode [part_number=1N4001 package="300 mil [THT]"]
  R1 = Resistor [tolerance=±5% resistance=10k package=THT]

nets:
  N1: WeMos_D1_Mini1.3V3, Q1.C, Q2.C
  N2: WeMos_D1_Mini1.D1, Q1.E, D1.anode
  N3: WeMos_D1_Mini1.D2, Q2.E, D2.anode
  N4: WeMos_D1_Mini1.G, R1.Pin_1
  N5: D1.cathode, D2.cathode, R1.Pin_0
